// Logisim project RISC_V_Single_Cycle.circ as structural Verilog: 5 circuits, main circuit main
module main (
);

  Register_4bit register_4bit_1 ();  // open: D, CLK, WE, in_4, o
endmodule

module Register_4bit (
  input  [3:0] D,
  input  CLK,
  input  WE,
  input  in_4,
  output [3:0] o
);

  wire d_ff_1_qn, d_ff_2_qn, d_ff_3_qn, multiplexer_1_out, multiplexer_2_out, multiplexer_3_out,
       multiplexer_4_out;

  Multiplexer multiplexer_1 (.in0(o[3]), .in1(D[3]), .out(multiplexer_1_out), .sel(WE));
  Multiplexer multiplexer_2 (.in0(o[2]), .in1(D[2]), .out(multiplexer_2_out), .sel(WE));
  Multiplexer multiplexer_3 (.in0(o[1]), .in1(D[1]), .out(multiplexer_3_out), .sel(WE));
  Multiplexer multiplexer_4 (.in0(o[0]), .in1(D[0]), .out(multiplexer_4_out), .sel(WE));
  D_Flip_Flop d_ff_1 (.D(multiplexer_1_out), .clk(CLK), .Q(o[3]), .Qn(d_ff_1_qn), .reset(in_4));  // open: preset
  D_Flip_Flop d_ff_2 (.D(multiplexer_2_out), .clk(CLK), .Q(o[2]), .Qn(d_ff_2_qn), .reset(in_4));  // open: preset
  D_Flip_Flop d_ff_3 (.D(multiplexer_3_out), .clk(CLK), .Q(o[1]), .Qn(d_ff_3_qn), .reset(in_4));  // open: preset
  D_Flip_Flop d_ff_4 (.D(multiplexer_4_out), .clk(CLK), .Q(o[0]), .reset(in_4));  // open: Qn, preset
endmodule

module Register_32bit (
  input  [31:0] D,
  input  CLK,
  input  WE,
  output [31:0] Q
);

  Register_4bit register_4bit_1 (.D(D[31:28]), .CLK(CLK), .WE(WE), .o(Q[31:28]));  // open: in_4
  Register_4bit register_4bit_2 (.D(D[27:24]), .CLK(CLK), .WE(WE), .o(Q[27:24]));  // open: in_4
  Register_4bit register_4bit_3 (.D(D[23:20]), .CLK(CLK), .WE(WE), .o(Q[23:20]));  // open: in_4
  Register_4bit register_4bit_4 (.D(D[19:16]), .CLK(CLK), .WE(WE), .o(Q[19:16]));  // open: in_4
  Register_4bit register_4bit_5 (.D(D[15:12]), .CLK(CLK), .WE(WE), .o(Q[15:12]));  // open: in_4
  Register_4bit register_4bit_6 (.D(D[11:8]), .CLK(CLK), .WE(WE), .o(Q[11:8]));  // open: in_4
  Register_4bit register_4bit_7 (.D(D[7:4]), .CLK(CLK), .WE(WE), .o(Q[7:4]));  // open: in_4
  Register_4bit register_4bit_8 (.D(D[3:0]), .CLK(CLK), .WE(WE), .o(Q[3:0]));  // open: in_4
endmodule

module Decoder_5to32 (
  input  WE,
  input  [4:0] WriteAddr
);

  wire decoder_1_out10, decoder_1_out16;

  Decoder #(.select(5)) decoder_1 (
    .out10(decoder_1_out10), .out16(decoder_1_out16), .out17(decoder_1_out16), .sel(WriteAddr), .en(WE));  // open: out0, out1, out2, out3, out4, out5, out6, out7, out8, out9, out11, out12, out13, out14, out15, out18, out19, out20, out21, out22, out23, out24, out25, out26, out27, out28, out29, out30, out31
endmodule

module Register_File (
  input  [4:0] ReadAddr1,
  input  [4:0] ReadAddr2,
  input  [4:0] WriteAddr,
  input  [31:0] WriteData,
  input  WE,
  input  CLK,
  output [31:0] ReadData1,
  output [31:0] ReadData2
);

  Register_32bit X1 ();  // open: D, CLK, WE, Q
endmodule
